// Logisim project Guia04.circ as structural Verilog: 13 circuits, main circuit main
module main (
  input  X,
  input  Y,
  input  Z,
  output out_4
);

  and and_1 (out_4, X, Y, Z);
endmodule

module _1a (
  input  x,
  input  y,
  input  z,
  output pora
);

  wire nor_1_out, not_1_out, not_2_out;

  not not_1 (not_1_out, y);
  not not_2 (not_2_out, x);
  nor nor_1 (nor_1_out, not_1_out, z);
  and and_1 (pora, not_2_out, nor_1_out);
endmodule

module _1b (
  input  x,
  input  y,
  input  z,
  output out
);

  wire nor_1_out, not_1_out, not_2_out;

  not not_1 (not_1_out, x);
  not not_2 (not_2_out, y);
  nor nor_1 (nor_1_out, not_1_out, not_2_out);
  and and_1 (out, nor_1_out, z);
endmodule

module _1c (
  input  x,
  input  y,
  input  z,
  output out
);

  wire nand_1_out, not_1_out, not_2_out;

  not not_1 (not_1_out, y);
  nand nand_1 (nand_1_out, x, not_1_out);
  not not_2 (not_2_out, z);
  and and_1 (out, nand_1_out, not_2_out);
endmodule

module _1d (
  input  x,
  input  y,
  input  z,
  output out
);

  wire nand_1_out, not_1_out;

  not not_1 (not_1_out, x);
  nand nand_1 (nand_1_out, not_1_out, y);
  and and_1 (out, nand_1_out, z);
endmodule

module _1e (
  input  x,
  input  y,
  input  z,
  output \or ,
  output out,
  output notOr
);

  wire not_1_out, not_2_out;

  not not_1 (not_1_out, x);
  not not_2 (not_2_out, y);
  or or_1 (\or , not_1_out, y);
  and and_1 (out, \or , notOr);
  nor nor_1 (notOr, not_2_out, z);
endmodule

module _1e_Simplificado_Deu_ruim (
  input  x,
  input  y,
  input  z,
  output out
);

  wire not_1_out;

  not not_1 (not_1_out, z);
  and and_1 (out, y, not_1_out);
endmodule

module _2a (
  input  x,
  input  y,
  input  x1,
  input  y1,
  output out,
  output out1
);

  wire nor_1_out, not_1_out, not_2_out;

  not not_1 (not_1_out, x);
  nor nor_1 (nor_1_out, not_1_out, y);
  not not_2 (not_2_out, y1);
  and and_1 (out, x, nor_1_out);
  and and_2 (out1, x1, not_2_out);
endmodule

module _2b (
  input  x,
  input  y,
  output out
);

  wire and_1_out, not_1_out, not_2_out;

  not not_1 (not_1_out, x);
  not not_2 (not_2_out, x);
  and and_1 (and_1_out, not_2_out, y);
  or or_1 (out, not_1_out, y, and_1_out);
endmodule

module _2b_Simplificado (
  input  x1,
  input  y1,
  output out1
);

  wire not_1_out;

  not not_1 (not_1_out, x1);
  or or_1 (out1, not_1_out, y1);
endmodule

module _2c (
  input  x,
  input  y,
  output out
);

  wire nand_1_out, not_1_out, not_2_out, or_1_out;

  not not_1 (not_1_out, x);
  not not_2 (not_2_out, y);
  nand nand_1 (nand_1_out, not_1_out, not_2_out);
  or or_1 (or_1_out, x, y);
  and and_1 (out, nand_1_out, or_1_out);
endmodule

module _2d (
  input  x,
  input  y,
  output out
);

  wire nand_1_out, nor_1_out, not_1_out, not_2_out;

  not not_1 (not_1_out, x);
  not not_2 (not_2_out, x);
  nand nand_1 (nand_1_out, not_1_out, y);
  nor nor_1 (nor_1_out, not_2_out, y);
  or or_1 (out, nand_1_out, nor_1_out);
endmodule

module _2e (
  input  x,
  input  y,
  output r
);

  wire nor_1_out, not_1_out, not_2_out, or_1_out;

  not not_1 (not_1_out, x);
  not not_2 (not_2_out, y);
  or or_1 (or_1_out, y, not_1_out);
  nor nor_1 (nor_1_out, not_2_out, x);
  and and_1 (r, or_1_out, nor_1_out);
endmodule
