// Logisim project Guia_05.circ as structural Verilog: 8 circuits, main circuit Q01
module Q01 (
  input  a,
  input  b,
  output out_3
);

  wire nor_1_out;

  nor nor_1 (nor_1_out, b, b);
  nor nor_2 (out_3, nor_1_out, a);
endmodule

module Q02 (
  input  a,
  input  b,
  output out_3
);

  wire nand_1_out;

  nand nand_1 (nand_1_out, a, a);
  nand nand_2 (out_3, nand_1_out, b);
endmodule

module Q03 (
  input  a,
  input  b,
  output out_3
);

  wire nor_1_out;

  nor nor_1 (nor_1_out, a, a);
  nor nor_2 (out_3, nor_1_out, b);
endmodule

module Q04 (
  input  a,
  input  b,
  output out_3
);

  wire nand_1_out;

  nand nand_1 (nand_1_out, a, a);
  nand nand_2 (out_3, nand_1_out, b);
endmodule

module Q05 (
  input  a,
  input  b,
  output out_3
);

  wire nor_1_out, nor_2_out, nor_3_out, nor_4_out;

  nor nor_1 (nor_1_out, a, a);
  nor nor_2 (nor_2_out, b, b);
  nor nor_3 (nor_3_out, b, nor_1_out);
  nor nor_4 (nor_4_out, a, nor_2_out);
  nor nor_5 (out_3, nor_3_out, nor_4_out);

  // Notes on the sheet:
  //   a xnor b == ~(a xor b) == (~a nor b) nor (a nor ~b)
endmodule

module Q06 (
  input  a,
  input  b,
  output out_3
);

  wire nand_1_out, nand_2_out, nand_3_out, nand_4_out;

  nand nand_1 (nand_1_out, b, b);
  nand nand_2 (nand_2_out, a, a);
  nand nand_3 (nand_3_out, a, nand_1_out);
  nand nand_4 (nand_4_out, b, nand_2_out);
  nand nand_5 (out_3, nand_3_out, nand_4_out);

  // Notes on the sheet:
  //   a xor b == (a nand b') nand (a' nand b)
endmodule

module Q07 (
  input  a,
  input  b,
  output out_3
);

  wire nor_1_out, nor_2_out, nor_3_out, nor_4_out;

  nor nor_1 (nor_1_out, b, b);
  nor nor_2 (nor_2_out, a, a);
  nor nor_3 (nor_3_out, nor_1_out, nor_2_out);
  nor nor_4 (nor_4_out, b, a);
  nor nor_5 (out_3, nor_3_out, nor_4_out);

  // Notes on the sheet:
  //   a' ^ b' == a^b == (a' nor b') nor (a nor b)
endmodule

module Q08 (
  input  a,
  input  b,
  output out_3
);

  wire nand_1_out;

  nand nand_1 (nand_1_out, a, b);
  nand nand_2 (out_3, nand_1_out, nand_1_out);

  // Notes on the sheet:
  //   (a'+b')' == a.b
endmodule
