// Logisim project Guia_06.circ as structural Verilog: 26 circuits, main circuit 01.a
module _01_a (
  input  x,
  input  y,
  input  z,
  output s
);

  wire and_1_out, and_2_out, not_1_out, not_2_out;

  not not_1 (not_1_out, x);
  not not_2 (not_2_out, y);
  and and_1 (and_1_out, not_1_out, not_2_out, z);
  and and_2 (and_2_out, x, y);
  or or_1 (s, and_1_out, and_2_out);
endmodule

module _01_b (
  input  x,
  input  y,
  input  z,
  output s
);

  wire and_1_out, and_2_out, not_1_out, not_2_out;

  not not_1 (not_1_out, z);
  not not_2 (not_2_out, z);
  and and_1 (and_1_out, y, not_1_out);
  and and_2 (and_2_out, x, not_2_out);
  or or_1 (s, and_1_out, and_2_out);
endmodule

module _01_c (
  input  x,
  input  y,
  input  z,
  output s
);

  wire and_1_out, and_2_out, not_1_out, not_2_out;

  not not_1 (not_1_out, y);
  not not_2 (not_2_out, z);
  and and_1 (and_1_out, not_1_out, z);
  and and_2 (and_2_out, y, not_2_out);
  or or_1 (s, and_1_out, and_2_out);
endmodule

module _01_d (
  input  x,
  input  y,
  input  z,
  output s
);

  wire and_1_out, and_2_out, and_3_out, not_1_out, not_2_out, not_3_out, not_4_out;

  not not_1 (not_1_out, y);
  not not_2 (not_2_out, x);
  not not_3 (not_3_out, z);
  not not_4 (not_4_out, y);
  and and_1 (and_1_out, not_1_out, z);
  and and_2 (and_2_out, not_2_out, y, not_3_out);
  and and_3 (and_3_out, x, not_4_out);
  or or_1 (s, and_1_out, and_2_out, and_3_out);
endmodule

module _01_e (
  input  x,
  input  y,
  input  z,
  output s
);

  wire and_1_out, and_2_out, and_3_out, not_1_out, not_2_out, not_3_out;

  not not_1 (not_1_out, x);
  not not_2 (not_2_out, y);
  not not_3 (not_3_out, z);
  and and_1 (and_1_out, not_1_out, not_2_out, not_3_out);
  and and_2 (and_2_out, y, z);
  and and_3 (and_3_out, x, y);
  or or_1 (s, and_1_out, and_2_out, and_3_out);
endmodule

module _02_a (
  input  x,
  input  y,
  input  z,
  output s
);

  wire not_1_out, not_2_out, not_3_out, or_1_out, or_2_out;

  not not_1 (not_1_out, z);
  not not_2 (not_2_out, x);
  not not_3 (not_3_out, z);
  or or_1 (or_1_out, y, not_1_out);
  or or_2 (or_2_out, not_2_out, not_3_out);
  and and_1 (s, or_1_out, or_2_out);
endmodule

module _02_b (
  input  x,
  input  y,
  input  z,
  output s
);

  wire and_1_out, not_1_out;

  not not_1 (not_1_out, x);
  and and_1 (and_1_out, not_1_out, y);
  or or_1 (s, z, and_1_out);
endmodule

module _02_c (
  input  x,
  input  y,
  input  z,
  output s
);

  wire and_1_out, and_2_out, not_1_out, not_2_out;

  not not_1 (not_1_out, y);
  not not_2 (not_2_out, z);
  and and_1 (and_1_out, not_1_out, not_2_out);
  and and_2 (and_2_out, x, y);
  or or_1 (s, and_1_out, and_2_out);
endmodule

module _02_d (
  input  x,
  input  y,
  input  z,
  output s
);

  wire and_1_out, and_2_out, not_1_out, not_2_out;

  not not_1 (not_1_out, y);
  not not_2 (not_2_out, z);
  and and_1 (and_1_out, not_1_out, z);
  and and_2 (and_2_out, y, not_2_out);
  or or_1 (s, and_1_out, and_2_out);
endmodule

module _02_e (
  input  x,
  input  y,
  input  z,
  output s
);

  not not_1 (s, y);
endmodule

module _03_a (
  input  x,
  input  y,
  input  w,
  input  z,
  output s
);

  wire and_1_out, and_2_out, and_3_out, and_4_out, not_1_out, not_2_out, not_3_out, not_4_out, not_5_out,
       not_6_out, not_7_out, not_8_out;

  not not_1 (not_1_out, x);
  not not_2 (not_2_out, w);
  not not_3 (not_3_out, x);
  not not_4 (not_4_out, y);
  not not_5 (not_5_out, z);
  not not_6 (not_6_out, w);
  not not_7 (not_7_out, z);
  not not_8 (not_8_out, w);
  and and_1 (and_1_out, not_1_out, not_2_out, z);
  and and_2 (and_2_out, not_3_out, not_4_out, w, not_5_out);
  and and_3 (and_3_out, x, not_6_out, not_7_out);
  and and_4 (and_4_out, x, y, not_8_out);
  or or_1 (s, and_1_out, and_2_out, and_3_out, and_4_out);
endmodule

module _03_b (
  input  x,
  input  y,
  input  w,
  input  z,
  output s
);

  wire and_1_out, and_2_out, and_3_out, not_1_out, not_2_out, not_3_out, not_4_out;

  not not_1 (not_1_out, x);
  and and_1 (and_1_out, not_1_out, not_2_out, not_3_out);
  not not_2 (not_2_out, y);
  not not_3 (not_3_out, w);
  not not_4 (not_4_out, x);
  and and_2 (and_2_out, not_4_out, z);
  and and_3 (and_3_out, y, z);
  or or_1 (s, and_1_out, and_2_out, and_3_out);
endmodule

module _03_c (
  input  x,
  input  y,
  input  w,
  input  z,
  output s
);

  wire and_1_out, and_2_out, and_3_out, not_1_out, not_2_out, not_3_out, not_4_out;

  not not_1 (not_1_out, x);
  not not_2 (not_2_out, y);
  and and_1 (and_1_out, not_1_out, not_2_out, not_3_out);
  not not_3 (not_3_out, w);
  and and_2 (and_2_out, w, not_4_out);
  not not_4 (not_4_out, z);
  and and_3 (and_3_out, y, w);
  or or_1 (s, and_1_out, and_2_out, and_3_out);
endmodule

module _03_d (
  input  x,
  input  y,
  input  w,
  input  z,
  output s
);

  wire and_1_out, and_2_out, and_3_out, not_1_out, not_2_out, not_3_out;

  and and_1 (and_1_out, w, not_1_out);
  not not_1 (not_1_out, z);
  not not_2 (not_2_out, x);
  and and_2 (and_2_out, not_2_out, y, not_3_out);
  not not_3 (not_3_out, z);
  and and_3 (and_3_out, y, w);
  or or_1 (s, and_1_out, and_2_out, and_3_out);
endmodule

module _03_e (
  input  x,
  input  y,
  input  w,
  input  z,
  output s
);

  wire and_1_out, and_2_out, and_3_out, and_4_out, not_1_out, not_2_out, not_3_out, not_4_out, not_5_out;

  not not_1 (not_1_out, y);
  and and_1 (and_1_out, not_1_out, not_2_out);
  not not_2 (not_2_out, w);
  not not_3 (not_3_out, y);
  and and_2 (and_2_out, not_3_out, z);
  not not_4 (not_4_out, x);
  and and_3 (and_3_out, not_4_out, w, z);
  not not_5 (not_5_out, w);
  and and_4 (and_4_out, x, not_5_out, z);
  or or_1 (s, and_1_out, and_2_out, and_3_out, and_4_out);
endmodule

module _04_a (
  input  x,
  input  y,
  input  w,
  input  z,
  output s
);

  wire not_1_out, not_2_out, not_3_out, not_4_out, not_5_out, or_1_out, or_2_out, or_3_out;

  or or_1 (or_1_out, x, not_1_out, z);
  not not_1 (not_1_out, w);
  or or_2 (or_2_out, x, not_2_out, not_3_out);
  not not_2 (not_2_out, y);
  not not_3 (not_3_out, w);
  not not_4 (not_4_out, y);
  or or_3 (or_3_out, not_4_out, not_5_out, z);
  not not_5 (not_5_out, w);
  and and_1 (s, or_1_out, or_2_out, or_3_out);
endmodule

module _04_b (
  input  x,
  input  y,
  input  w,
  input  z,
  output s
);

  wire and_1_out, and_2_out, and_3_out, and_4_out, and_5_out, not_1_out, not_2_out, not_3_out, not_4_out,
       not_5_out, not_6_out, not_7_out;

  not not_1 (not_1_out, x);
  and and_1 (and_1_out, not_1_out, not_2_out);
  not not_2 (not_2_out, y);
  not not_3 (not_3_out, y);
  and and_2 (and_2_out, not_3_out, not_4_out);
  not not_4 (not_4_out, z);
  not not_5 (not_5_out, x);
  and and_3 (and_3_out, not_5_out, w);
  and and_4 (and_4_out, w, z);
  and and_5 (and_5_out, x, not_6_out, not_7_out);
  not not_6 (not_6_out, w);
  not not_7 (not_7_out, z);
  or or_1 (s, and_1_out, and_2_out, and_3_out, and_4_out, and_5_out);
endmodule

module _04_c (
  input  x,
  input  y,
  input  w,
  input  z,
  output s
);

  wire and_1_out, and_2_out, and_3_out, and_4_out, and_5_out, and_6_out, and_7_out, not_1_out, not_2_out,
       not_3_out, not_4_out, not_5_out, not_6_out, not_7_out, not_8_out, not_9_out, not_10_out;

  not not_1 (not_1_out, x);
  not not_2 (not_2_out, y);
  not not_3 (not_3_out, x);
  not not_4 (not_4_out, w);
  not not_5 (not_5_out, y);
  not not_6 (not_6_out, x);
  not not_7 (not_7_out, z);
  not not_8 (not_8_out, y);
  not not_9 (not_9_out, w);
  not not_10 (not_10_out, z);
  and and_1 (and_1_out, not_1_out, not_2_out);
  and and_2 (and_2_out, not_3_out, not_4_out, z);
  and and_3 (and_3_out, not_5_out, z);
  and and_4 (and_4_out, not_6_out, w, not_7_out);
  and and_5 (and_5_out, not_8_out, w);
  and and_6 (and_6_out, x, w, z);
  and and_7 (and_7_out, x, y, not_9_out, not_10_out);
  or or_1 (s, and_1_out, and_2_out, and_3_out, and_4_out, and_5_out, and_6_out, and_7_out);
endmodule

module _04_d (
  input  x,
  input  y,
  input  w,
  input  z,
  output s
);

  wire and_1_out, and_2_out, and_3_out, and_4_out, not_1_out, not_2_out, not_3_out, not_4_out, not_5_out,
       not_6_out;

  not not_1 (not_1_out, y);
  and and_1 (and_1_out, not_1_out, not_2_out);
  not not_2 (not_2_out, z);
  not not_3 (not_3_out, w);
  and and_2 (and_2_out, not_3_out, not_4_out);
  not not_4 (not_4_out, z);
  not not_5 (not_5_out, x);
  and and_3 (and_3_out, not_5_out, w);
  and and_4 (and_4_out, x, y, not_6_out);
  not not_6 (not_6_out, w);
  or or_1 (s, and_1_out, and_2_out, and_3_out, and_4_out);
endmodule

module _04_e (
  input  x,
  input  y,
  input  w,
  input  z,
  output s
);

  wire and_1_out, and_2_out, and_3_out, and_4_out, not_1_out, not_2_out, not_3_out, not_4_out, not_5_out,
       not_6_out, not_7_out;

  not not_1 (not_1_out, y);
  and and_1 (and_1_out, not_1_out, not_2_out);
  not not_2 (not_2_out, w);
  not not_3 (not_3_out, w);
  and and_2 (and_2_out, not_3_out, not_4_out);
  not not_4 (not_4_out, z);
  not not_5 (not_5_out, x);
  not not_6 (not_6_out, y);
  and and_3 (and_3_out, not_5_out, not_6_out, z);
  and and_4 (and_4_out, x, not_7_out);
  not not_7 (not_7_out, z);
  or or_1 (s, and_1_out, and_2_out, and_3_out, and_4_out);
endmodule

module _05_Original (
  input  x,
  input  y,
  input  z,
  output s
);

  wire and_1_out, and_2_out, and_3_out, not_1_out, not_2_out, not_3_out, not_4_out, not_5_out, or_1_out,
       or_2_out;

  not not_1 (not_1_out, y);
  not not_2 (not_2_out, x);
  or or_1 (or_1_out, not_1_out, not_2_out);
  and and_1 (and_1_out, y, x);
  and and_2 (and_2_out, z, y);
  or or_2 (or_2_out, and_2_out, not_3_out);
  not not_3 (not_3_out, x);
  not not_4 (not_4_out, or_1_out);
  and and_3 (and_3_out, not_4_out, not_5_out);
  not not_5 (not_5_out, and_1_out);
  or or_3 (s, and_3_out, or_2_out);
endmodule

module _06_Original (
  input  x,
  input  y,
  input  w,
  input  z,
  output s
);

  wire and_1_out, and_2_out, and_3_out, not_1_out, not_2_out, not_3_out, not_4_out, not_5_out, not_6_out,
       not_7_out, or_1_out, or_2_out;

  not not_1 (not_1_out, y);
  or or_1 (or_1_out, not_1_out, w, not_2_out);
  not not_2 (not_2_out, x);
  not not_3 (not_3_out, w);
  and and_1 (and_1_out, y, not_3_out, x);
  and and_2 (and_2_out, z, w, y);
  not not_4 (not_4_out, x);
  not not_5 (not_5_out, or_1_out);
  not not_6 (not_6_out, and_1_out);
  not not_7 (not_7_out, or_2_out);
  or or_2 (or_2_out, and_2_out, not_4_out);
  and and_3 (and_3_out, not_5_out, not_6_out);
  or or_3 (s, and_3_out, not_7_out);
endmodule

module _06_Simplificado (
  input  x,
  input  y,
  input  w,
  input  z,
  output s
);

  wire not_1_out, not_2_out, not_3_out, or_1_out;

  not not_1 (not_1_out, z);
  not not_2 (not_2_out, w);
  not not_3 (not_3_out, y);
  or or_1 (or_1_out, not_1_out, not_2_out, not_3_out);
  and and_1 (s, x, or_1_out);
endmodule

module _05_Simplificado (
  input  x,
  input  y,
  input  z,
  output s
);

  wire and_1_out, not_1_out;

  not not_1 (not_1_out, x);
  and and_1 (and_1_out, z, y);
  or or_1 (s, not_1_out, and_1_out);
endmodule

module _07 (
  input  x,
  input  y,
  input  z,
  output s
);

  wire not_1_out, not_2_out, or_1_out, or_2_out;

  not not_1 (not_1_out, y);
  not not_2 (not_2_out, x);
  or or_1 (or_1_out, x, not_1_out, z);
  or or_2 (or_2_out, not_2_out, y, z);
  and and_1 (s, or_1_out, or_2_out);
endmodule

module _08 (
  input  w,
  input  x,
  input  y,
  input  z,
  output s
);

  wire and_1_out, and_2_out, and_3_out, and_4_out, not_1_out, not_2_out, not_3_out, not_4_out, not_5_out,
       not_6_out;

  not not_1 (not_1_out, y);
  not not_2 (not_2_out, x);
  not not_3 (not_3_out, y);
  not not_4 (not_4_out, w);
  not not_5 (not_5_out, x);
  not not_6 (not_6_out, z);
  and and_1 (and_1_out, w, x, y, z);
  and and_2 (and_2_out, w, x, not_1_out, z);
  and and_3 (and_3_out, w, not_2_out, not_3_out, z);
  and and_4 (and_4_out, not_4_out, not_5_out, y, not_6_out);
  or or_1 (s, and_1_out, and_2_out, and_3_out, and_4_out);
endmodule
