// Logisim project Guia_07.circ as structural Verilog: 10 circuits, main circuit 01.
module MUX2x1 (
  input  a,
  input  b,
  input  selector,
  output out_4
);

  wire and_1_out, and_2_out, not_1_out;

  not not_1 (not_1_out, selector);
  and and_1 (and_1_out, a, not_1_out);
  or or_1 (out_4, and_1_out, and_2_out);
  and and_2 (and_2_out, b, selector);
endmodule

module MUX4x1 (
  input  a,
  input  b,
  input  c,
  input  d,
  input  [1:0] selector,
  output out_6
);

  wire _00_out, _01_out, _10_out, _11_out, not_1_out, not_2_out, not_3_out, not_4_out;

  and _00 (_00_out, a, not_1_out, not_2_out);
  not not_1 (not_1_out, selector[0]);
  not not_2 (not_2_out, selector[1]);
  and _01 (_01_out, b, selector[0], not_3_out);
  not not_3 (not_3_out, selector[1]);
  not not_4 (not_4_out, selector[0]);
  and _10 (_10_out, c, not_4_out, selector[1]);
  and _11 (_11_out, d, selector[0], selector[1]);
  or or_1 (out_6, _00_out, _01_out, _10_out, _11_out);
endmodule

module MUX8x1 (
  input  [2:0] in_1,
  input  _0,
  input  _1,
  input  _2,
  input  _3,
  input  _4,
  input  _5,
  input  _6,
  input  _7,
  output out_10
);

  wire _0_out, _1_out, _2_out, _3_out, _4_out, _5_out, _6_out, _7_out, not_1_out, not_2_out, not_3_out,
       not_4_out, not_5_out, not_6_out, not_7_out, not_8_out, not_9_out, not_10_out, not_11_out, not_12_out;

  not not_1 (not_1_out, in_1[2]);
  not not_2 (not_2_out, in_1[1]);
  not not_3 (not_3_out, in_1[0]);
  not not_4 (not_4_out, in_1[2]);
  not not_5 (not_5_out, in_1[1]);
  not not_6 (not_6_out, in_1[2]);
  not not_7 (not_7_out, in_1[0]);
  not not_8 (not_8_out, in_1[2]);
  not not_9 (not_9_out, in_1[1]);
  not not_10 (not_10_out, in_1[0]);
  not not_11 (not_11_out, in_1[1]);
  not not_12 (not_12_out, in_1[0]);
  and u__0 (_0_out, not_1_out, not_2_out, not_3_out, _0);
  and u__1 (_1_out, not_4_out, not_5_out, in_1[0], _1);
  and u__2 (_2_out, not_6_out, in_1[1], not_7_out, _2);
  and u__3 (_3_out, not_8_out, in_1[1], in_1[0], _3);
  and u__4 (_4_out, in_1[2], not_9_out, not_10_out, _4);
  and u__5 (_5_out, in_1[2], not_11_out, in_1[0], _5);
  and u__6 (_6_out, in_1[2], in_1[1], not_12_out, _6);
  and u__7 (_7_out, in_1[2], in_1[1], in_1[0], _7);
  or or_1 (out_10, _0_out, _1_out, _2_out, _3_out, _4_out, _5_out, _6_out, _7_out);
endmodule

module _01 (
  input  in_1,
  input  in_2,
  input  a,
  input  b,
  input  c,
  output out_6,
  output out_7,
  output s
);

  wire and_2_out, and_3_out, and_4_out, nand_2_out, not_1_out;

  and and_1 (out_6, in_1, in_2);
  nand nand_1 (out_7, in_1, in_2);
  and and_2 (and_2_out, a, b);
  nand nand_2 (nand_2_out, b, a);
  and and_3 (and_3_out, and_2_out, not_1_out);
  not not_1 (not_1_out, c);
  and and_4 (and_4_out, c, nand_2_out);
  or or_1 (s, and_3_out, and_4_out);
endmodule

module _02 (
  input  a,
  input  b,
  input  c,
  output s
);

  wire and_1_out, and_2_out, nor_1_out, not_1_out, or_1_out;

  or or_1 (or_1_out, a, b);
  nor nor_1 (nor_1_out, b, a);
  and and_1 (and_1_out, or_1_out, not_1_out);
  not not_1 (not_1_out, c);
  and and_2 (and_2_out, c, nor_1_out);
  or or_2 (s, and_1_out, and_2_out);
endmodule

module _03 (
  input  a,
  input  b,
  input  sel1,
  input  sel2,
  output s
);

  wire and_1_out, mux2x1_1_out_4, mux2x1_2_out_4, nand_1_out, nor_1_out, or_1_out;

  and and_1 (and_1_out, a, b);
  nand nand_1 (nand_1_out, a, b);
  or or_1 (or_1_out, a, b);
  nor nor_1 (nor_1_out, a, b);
  MUX2x1 mux2x1_1 (.selector(sel1), .out_4(mux2x1_1_out_4), .a(and_1_out), .b(nand_1_out));
  MUX2x1 mux2x1_2 (.selector(sel1), .out_4(mux2x1_2_out_4), .a(or_1_out), .b(nor_1_out));
  MUX2x1 mux2x1_3 (.selector(sel2), .out_4(s), .a(mux2x1_1_out_4), .b(mux2x1_2_out_4));
endmodule

module _04 (
  input  a,
  input  b,
  input  sel1,
  input  sel2,
  output s
);

  wire nor_1_out, or_1_out, xnor_1_out, xor_1_out;

  nor nor_1 (nor_1_out, a, b);
  or or_1 (or_1_out, a, b);
  xor xor_1 (xor_1_out, a, b);
  xnor xnor_1 (xnor_1_out, a, b);
  MUX4x1 mux4x1_1 (.selector({sel1, sel2}), .out_6(s), .a(nor_1_out), .b(or_1_out), .c(xor_1_out), .d(xnor_1_out));
endmodule

module _05 (
  input  a,
  input  b,
  input  sel1,
  input  sel2,
  input  sel3,
  output out_6
);

  wire and_1_out, nand_1_out, nor_1_out, not_1_out, not_2_out, or_1_out, xnor_1_out, xor_1_out;

  not not_1 (not_1_out, a);
  not not_2 (not_2_out, b);
  or or_1 (or_1_out, a, b);
  nor nor_1 (nor_1_out, a, b);
  and and_1 (and_1_out, a, b);
  nand nand_1 (nand_1_out, a, b);
  xor xor_1 (xor_1_out, a, b);
  xnor xnor_1 (xnor_1_out, a, b);
  MUX8x1 mux8x1_1 (
    .in_1({sel1, sel2, sel3}), .out_10(out_6), ._0(not_1_out), ._1(not_2_out), ._2(or_1_out), ._3(nor_1_out),
    ._4(and_1_out), ._5(nand_1_out), ._6(xor_1_out), ._7(xnor_1_out));
endmodule

module Igualdade_2bits (
  input  [1:0] a,
  input  [1:0] b,
  output out_3
);

  wire xnor_1_out, xnor_2_out;

  xnor xnor_1 (xnor_1_out, a[0], b[0]);
  and and_1 (out_3, xnor_1_out, xnor_2_out);
  xnor xnor_2 (xnor_2_out, a[1], b[1]);
endmodule

module _06 (
  input  [1:0] a,
  input  [1:0] b,
  input  _1_Igual_0_Diferente,
  output out_4
);

  wire igualdade_2bits_1_out_3, not_1_out;

  Igualdade_2bits igualdade_2bits_1 (.a(a), .b(b), .out_3(igualdade_2bits_1_out_3));
  MUX2x1 mux2x1_1 (.selector(_1_Igual_0_Diferente), .out_4(out_4), .a(igualdade_2bits_1_out_3), .b(not_1_out));
  not not_1 (not_1_out, igualdade_2bits_1_out_3);
endmodule
