// Logisim project Guia_08.circ as structural Verilog: 20 circuits, main circuit +/2
module _2 (
  input  a,
  input  b,
  output soma,
  output vai1
);

  xor xor_1 (soma, a, b);
  and and_1 (vai1, a, b);
endmodule

module circuit (
  input  a,
  input  b,
  input  vem1,
  output saida,
  output vai1
);

  wire n2_1_soma, n2_1_vai1, n2_2_vai1;

  _2 u_2_1 (.a(a), .b(b), .soma(n2_1_soma), .vai1(n2_1_vai1));
  _2 u_2_2 (.a(n2_1_soma), .b(vem1), .soma(saida), .vai1(n2_2_vai1));
  or or_1 (vai1, n2_2_vai1, n2_1_vai1);
endmodule

module _5 (
  input  [4:0] a,
  input  [4:0] b,
  output [5:0] out_3
);

  wire n2_1_vai1, part_1_vai1, part_2_vai1, part_3_vai1;

  _2 u_2_1 (.a(a[0]), .b(b[0]), .soma(out_3[0]), .vai1(n2_1_vai1));
  circuit part_1 (.a(a[1]), .b(b[1]), .vem1(n2_1_vai1), .saida(out_3[1]), .vai1(part_1_vai1));
  circuit part_2 (.a(a[2]), .b(b[2]), .vem1(part_1_vai1), .saida(out_3[2]), .vai1(part_2_vai1));
  circuit part_3 (.a(a[3]), .b(b[3]), .vem1(part_2_vai1), .saida(out_3[3]), .vai1(part_3_vai1));
  circuit part_4 (.a(a[4]), .b(b[4]), .vem1(part_3_vai1), .saida(out_3[4]), .vai1(out_3[5]));
endmodule

module _6 (
  input  [5:0] a,
  input  [5:0] b,
  output [6:0] out_3
);

  wire n2_1_vai1, part_1_vai1, part_2_vai1, part_3_vai1, part_4_vai1;

  _2 u_2_1 (.a(a[0]), .b(b[0]), .soma(out_3[0]), .vai1(n2_1_vai1));
  circuit part_1 (.a(a[1]), .b(b[1]), .vem1(n2_1_vai1), .saida(out_3[1]), .vai1(part_1_vai1));
  circuit part_2 (.a(a[2]), .b(b[2]), .vem1(part_1_vai1), .saida(out_3[2]), .vai1(part_2_vai1));
  circuit part_3 (.a(a[3]), .b(b[3]), .vem1(part_2_vai1), .saida(out_3[3]), .vai1(part_3_vai1));
  circuit part_4 (.a(a[4]), .b(b[4]), .vem1(part_3_vai1), .saida(out_3[4]), .vai1(part_4_vai1));
  circuit part_5 (.a(a[5]), .b(b[5]), .vem1(part_4_vai1), .saida(out_3[5]), .vai1(out_3[6]));
endmodule

module _2_2 (
  input  a,
  input  b,
  output out_3,
  output out_4
);

  wire not_1_out;

  xor xor_1 (out_3, a, b);
  and and_1 (out_4, b, not_1_out);
  not not_1 (not_1_out, a);
endmodule

module circuit_2 (
  input  vem_um,
  input  a,
  input  b,
  output saida,
  output out_5
);

  wire n2_1_out_3, n2_1_out_4, n2_2_out_4;

  _2_2 u_2_1 (.a(a), .b(b), .out_3(n2_1_out_3), .out_4(n2_1_out_4));
  _2_2 u_2_2 (.a(n2_1_out_3), .b(vem_um), .out_3(saida), .out_4(n2_2_out_4));
  or or_1 (out_5, n2_2_out_4, n2_1_out_4);
endmodule

module C2_6 (
  input  [5:0] a,
  output [5:0] C2_a
);

  wire [5:0] not_1_out;
  wire [6:6] n6_1_out_3;

  assign not_1_out = ~a;  // NOT_Gate not_1, 6 bits wide
  _6 u_6_1 (.a(not_1_out), .b(6'b000001), .out_3({n6_1_out_3[6], C2_a}));
  // Probe on n6_1_out_3[6]
endmodule

module _4bits (
  input  [3:0] a,
  input  [3:0] b,
  output out_3
);

  wire xnor_1_out, xnor_2_out, xnor_3_out, xnor_4_out;

  xnor xnor_1 (xnor_1_out, a[0], b[0]);
  xnor xnor_2 (xnor_2_out, a[1], b[1]);
  xnor xnor_3 (xnor_3_out, a[2], b[2]);
  xnor xnor_4 (xnor_4_out, a[3], b[3]);
  and and_1 (out_3, xnor_1_out, xnor_2_out, xnor_3_out, xnor_4_out);
endmodule

module _5bits (
  input  [4:0] a,
  input  [4:0] b,
  output out_3
);

  wire xnor_1_out, xnor_2_out, xnor_3_out, xnor_4_out, xnor_5_out;

  xnor xnor_1 (xnor_1_out, a[0], b[0]);
  xnor xnor_2 (xnor_2_out, a[1], b[1]);
  xnor xnor_3 (xnor_3_out, a[2], b[2]);
  xnor xnor_4 (xnor_4_out, a[3], b[3]);
  xnor xnor_5 (xnor_5_out, a[4], b[4]);
  and and_1 (out_3, xnor_1_out, xnor_2_out, xnor_3_out, xnor_4_out, xnor_5_out);
endmodule

module _4bits_2 (
  input  [3:0] a,
  input  [3:0] b,
  output out_3
);

  wire xor_1_out, xor_2_out, xor_3_out, xor_4_out;

  xor xor_1 (xor_1_out, a[0], b[0]);
  xor xor_2 (xor_2_out, a[1], b[1]);
  xor xor_3 (xor_3_out, a[2], b[2]);
  xor xor_4 (xor_4_out, a[3], b[3]);
  or or_1 (out_3, xor_1_out, xor_2_out, xor_3_out, xor_4_out);
endmodule

module _5bits_2 (
  input  [4:0] a,
  input  [4:0] b,
  output out_3
);

  wire xor_1_out, xor_2_out, xor_3_out, xor_4_out, xor_5_out;

  xor xor_1 (xor_1_out, a[0], b[0]);
  xor xor_2 (xor_2_out, a[1], b[1]);
  xor xor_3 (xor_3_out, a[2], b[2]);
  xor xor_4 (xor_4_out, a[3], b[3]);
  xor xor_5 (xor_5_out, a[4], b[4]);
  or or_1 (out_3, xor_1_out, xor_2_out, xor_3_out, xor_4_out, xor_5_out);
endmodule

module MUX2x1 (
  input  a,
  input  b,
  input  selector,
  output out_4
);

  wire and_1_out, and_2_out, not_1_out;

  and and_1 (and_1_out, a, not_1_out);
  not not_1 (not_1_out, selector);
  and and_2 (and_2_out, b, selector);
  or or_1 (out_4, and_1_out, and_2_out);
endmodule

module MUX2x1_5bits (
  input  [4:0] a,
  input  [4:0] b,
  input  selector,
  output [4:0] out_4
);

  wire [4:0] and_1_out, and_2_out, not_1_out;

  assign and_1_out = a & not_1_out;  // AND_Gate and_1, 5 bits wide
  assign not_1_out = ~{5{selector}};  // NOT_Gate not_1, 5 bits wide
  assign and_2_out = b & {5{selector}};  // AND_Gate and_2, 5 bits wide
  assign out_4 = and_1_out | and_2_out;  // OR_Gate or_1, 5 bits wide
endmodule

module _01 (
  input  [3:0] a,
  input  [3:0] b,
  output [4:0] out_3
);

  wire n2_1_vai1, part_1_vai1, part_2_vai1;

  _2 u_2_1 (.a(a[0]), .b(b[0]), .soma(out_3[0]), .vai1(n2_1_vai1));
  circuit part_1 (.a(a[1]), .b(b[1]), .vem1(n2_1_vai1), .saida(out_3[1]), .vai1(part_1_vai1));
  circuit part_2 (.a(a[2]), .b(b[2]), .vem1(part_1_vai1), .saida(out_3[2]), .vai1(part_2_vai1));
  circuit part_3 (.a(a[3]), .b(b[3]), .vem1(part_2_vai1), .saida(out_3[3]), .vai1(out_3[4]));
endmodule

module _02 (
  input  [3:0] a,
  input  [3:0] b,
  output [4:0] out_3
);

  wire n2_1_out_4, part_1_out_5, part_2_out_5;

  _2_2 u_2_1 (.a(a[0]), .b(b[0]), .out_3(out_3[0]), .out_4(n2_1_out_4));
  circuit_2 part_1 (.vem_um(n2_1_out_4), .a(a[1]), .b(b[1]), .saida(out_3[1]), .out_5(part_1_out_5));
  circuit_2 part_2 (.vem_um(part_1_out_5), .a(a[2]), .b(b[2]), .saida(out_3[2]), .out_5(part_2_out_5));
  circuit_2 part_3 (.vem_um(part_2_out_5), .a(a[3]), .b(b[3]), .saida(out_3[3]), .out_5(out_3[4]));
endmodule

module _03 (
  input  [3:0] a,
  input  [3:0] b,
  output out_3
);

  _4bits u_4bits_1 (.a(a), .b(b), .out_3(out_3));
endmodule

module _04 (
  input  [3:0] a,
  input  [3:0] b,
  output out_3
);

  _4bits_2 u_4bits_1 (.a(a), .b(b), .out_3(out_3));
endmodule

module _05 (
  input  [5:0] Entrada,
  output [5:0] Complemento_de_2,
  output [6:0] Prova_por_soma
);

  C2_6 c2_6_1 (.a(Entrada), .C2_a(Complemento_de_2));
  _6 u_6_1 (.a(Entrada), .b(Complemento_de_2), .out_3(Prova_por_soma));

  // Notes on the sheet:
  //   Î  Bit de overflow
endmodule

module _06 (
  input  [4:0] a,
  input  [4:0] b,
  input  in_3,
  output [5:0] s
);

  wire [4:0] mux2x1_5bits_1_out_4, not_1_out;
  wire [5:0] n5_1_out_3;

  assign not_1_out = ~b;  // NOT_Gate not_1, 5 bits wide
  _5 u_5_1 (.a(not_1_out), .b(5'b00001), .out_3(n5_1_out_3));
  // Probe on n5_1_out_3[5]
  _5 u_5_2 (.a(a), .b(mux2x1_5bits_1_out_4), .out_3(s));
  MUX2x1_5bits mux2x1_5bits_1 (.a(b), .b(n5_1_out_3[4:0]), .selector(in_3), .out_4(mux2x1_5bits_1_out_4));
endmodule

module _07 (
  input  [4:0] a,
  input  [4:0] b,
  input  sel,
  output out_4
);

  wire n5bits_1_out_3, n5bits_2_out_3;

  _5bits u_5bits_1 (.a(a), .b(b), .out_3(n5bits_1_out_3));
  _5bits_2 u_5bits_2 (.a(a), .b(b), .out_3(n5bits_2_out_3));
  MUX2x1 mux2x1_1 (.a(n5bits_1_out_3), .b(n5bits_2_out_3), .selector(sel), .out_4(out_4));
endmodule
