// Logisim project Guia_11.circ as structural Verilog: 8 circuits, main circuit Q01.
module Q01 (
  input  x,
  output out_2
);

  wire and_1_out, and_2_out, and_3_out, and_4_out, and_5_out, clock_1_out, not_1_out, not_2_out, not_3_out,
       not_4_out, not_5_out, not_6_out, not_7_out, or_1_out, or_2_out, q0_q, q1_q;

  Clock clock_1 (.out(clock_1_out));
  or or_1 (or_1_out, and_2_out, and_1_out);
  and and_1 (and_1_out, q1_q, not_4_out);
  and and_2 (and_2_out, not_1_out, q0_q, x);
  not not_1 (not_1_out, q1_q);
  D_Flip_Flop #(.Pre_Clr_Positions("LEGACY"), .enable("true"), .NewFFLayout("false")) q1 (
    .clk(clock_1_out), .D(or_1_out), .Q(q1_q));  // open: Qn, preset, en, reset
  and and_3 (and_3_out, not_3_out, not_2_out, x);
  not not_2 (not_2_out, q0_q);
  not not_3 (not_3_out, q1_q);
  not not_4 (not_4_out, q0_q);
  or or_2 (or_2_out, and_3_out, and_4_out, and_5_out);
  and and_4 (and_4_out, q1_q, not_5_out, not_6_out);
  and and_5 (and_5_out, q1_q, q0_q, x);
  not not_5 (not_5_out, q0_q);
  not not_6 (not_6_out, x);
  D_Flip_Flop #(.Pre_Clr_Positions("LEGACY"), .enable("true"), .NewFFLayout("false")) q0 (
    .clk(clock_1_out), .D(or_2_out), .Q(q0_q));  // open: Qn, preset, en, reset
  not not_7 (not_7_out, x);
  and and_6 (out_2, q0_q, q1_q, not_7_out);

  // Notes on the sheet:
  //   Sequencia: 110
endmodule

module Q02 (
  input  x,
  output Saida
);

  wire and_1_out, and_2_out, and_3_out, and_4_out, and_5_out, and_6_out, clk, not_1_out, not_2_out,
       not_3_out, not_4_out, not_5_out, not_6_out, not_7_out, not_8_out, not_9_out, not_10_out, not_11_out,
       not_12_out, not_13_out, not_14_out, or_1_out, or_2_out, q0, q1, q2;

  Clock clock_1 (.out(clk));
  and and_1 (and_1_out, not_1_out, q1, q0, x);
  not not_1 (not_1_out, q2);
  D_Flip_Flop #(.Pre_Clr_Positions("LEGACY"), .enable("true"), .NewFFLayout("false")) d_ff_1 (
    .clk(clk), .D(and_1_out), .Q(q2));  // open: Qn, preset, en, reset
  and and_2 (and_2_out, not_3_out, not_2_out, q0, x);
  not not_2 (not_2_out, q1);
  not not_3 (not_3_out, q2);
  or or_1 (or_1_out, and_2_out, and_3_out, and_4_out);
  and and_3 (and_3_out, not_4_out, q1, not_5_out);
  not not_4 (not_4_out, q2);
  not not_5 (not_5_out, q0);
  D_Flip_Flop #(.Pre_Clr_Positions("LEGACY"), .enable("true"), .NewFFLayout("false")) d_ff_2 (
    .clk(clk), .D(or_1_out), .Q(q1));  // open: Qn, preset, en, reset
  not not_6 (not_6_out, q2);
  and and_4 (and_4_out, q2, not_7_out, not_8_out, x);
  not not_7 (not_7_out, q1);
  not not_8 (not_8_out, q0);
  or or_2 (or_2_out, and_5_out, and_6_out);
  and and_5 (and_5_out, not_6_out, q1, not_10_out, not_9_out);
  not not_9 (not_9_out, x);
  not not_10 (not_10_out, q0);
  and and_6 (and_6_out, not_11_out, not_12_out, not_14_out, x);
  not not_11 (not_11_out, q2);
  not not_12 (not_12_out, q1);
  D_Flip_Flop #(.Pre_Clr_Positions("LEGACY"), .enable("true"), .NewFFLayout("false")) d_ff_3 (
    .clk(clk), .D(or_2_out), .Q(q0));  // open: Qn, preset, en, reset
  not not_13 (not_13_out, q2);
  not not_14 (not_14_out, q0);
  and and_7 (Saida, q0, q1, not_13_out, x);

  // Notes on the sheet:
  //   Sequencia correta: 1101
endmodule

module Q03 (
  input  x,
  input  x_2,
  output out_3,
  output Saida
);

  wire and_1_out, and_2_out, and_3_out, and_4_out, and_5_out, and_6_out, and_7_out, and_8_out, and_9_out,
       and_10_out, and_12_out, clk, clock_1_out, not_1_out, not_2_out, not_3_out, not_4_out, not_5_out,
       not_6_out, not_7_out, not_8_out, not_9_out, not_10_out, not_11_out, not_12_out, not_13_out,
       not_14_out, not_15_out, not_16_out, not_17_out, not_18_out, not_19_out, not_20_out, not_21_out,
       or_1_out, or_2_out, or_3_out, or_4_out, q0, q0_q, q1, q1_q, q2;

  not not_1 (not_1_out, q2);
  Clock clock_1 (.out(clock_1_out));
  or or_1 (or_1_out, and_1_out, and_2_out);
  and and_1 (and_1_out, not_2_out, q0_q, x);
  and and_2 (and_2_out, q1_q, not_6_out);
  not not_2 (not_2_out, q1_q);
  Clock clock_2 (.out(clk));
  D_Flip_Flop #(.Pre_Clr_Positions("LEGACY"), .enable("true"), .NewFFLayout("false")) d_ff_1 (
    .clk(clk), .D(and_3_out), .Q(q2));  // open: Qn, preset, en, reset
  and and_3 (and_3_out, not_1_out, q1, q0, x_2);
  and and_4 (and_4_out, not_4_out, not_3_out, q0, x_2);
  not not_3 (not_3_out, q1);
  not not_4 (not_4_out, q2);
  D_Flip_Flop #(.Pre_Clr_Positions("LEGACY"), .enable("true"), .NewFFLayout("false")) u_q1 (
    .clk(clock_1_out), .D(or_1_out), .Q(q1_q));  // open: Qn, preset, en, reset
  and and_5 (and_5_out, not_7_out, not_5_out, x);
  not not_5 (not_5_out, q0_q);
  not not_6 (not_6_out, q0_q);
  not not_7 (not_7_out, q1_q);
  or or_2 (or_2_out, and_4_out, and_6_out, and_9_out);
  and and_6 (and_6_out, not_8_out, q1, not_11_out);
  not not_8 (not_8_out, q2);
  or or_3 (or_3_out, and_5_out, and_8_out, and_7_out);
  and and_7 (and_7_out, q1_q, q0_q, x);
  and and_8 (and_8_out, q1_q, not_9_out, not_10_out);
  not not_9 (not_9_out, q0_q);
  not not_10 (not_10_out, x);
  D_Flip_Flop #(.Pre_Clr_Positions("LEGACY"), .enable("true"), .NewFFLayout("false")) d_ff_2 (
    .clk(clk), .D(or_2_out), .Q(q1));  // open: Qn, preset, en, reset
  not not_11 (not_11_out, q0);
  and and_9 (and_9_out, q2, not_13_out, not_12_out, x_2);
  not not_12 (not_12_out, q0);
  not not_13 (not_13_out, q1);
  D_Flip_Flop #(.Pre_Clr_Positions("LEGACY"), .enable("true"), .NewFFLayout("false")) u_q0 (
    .clk(clock_1_out), .D(or_3_out), .Q(q0_q));  // open: Qn, preset, en, reset
  not not_14 (not_14_out, x);
  or or_4 (or_4_out, and_10_out, and_12_out);
  and and_10 (and_10_out, not_16_out, q1, not_17_out, not_15_out);
  not not_15 (not_15_out, x_2);
  not not_16 (not_16_out, q2);
  not not_17 (not_17_out, q0);
  not not_18 (not_18_out, q2);
  and and_11 (out_3, q0_q, q1_q, not_14_out);
  D_Flip_Flop #(.Pre_Clr_Positions("LEGACY"), .enable("true"), .NewFFLayout("false")) d_ff_3 (
    .clk(clk), .D(or_4_out), .Q(q0));  // open: Qn, preset, en, reset
  and and_12 (and_12_out, not_18_out, not_20_out, not_19_out, x_2);
  not not_19 (not_19_out, q0);
  not not_20 (not_20_out, q1);
  not not_21 (not_21_out, q2);
  and and_13 (Saida, q0, q1, not_21_out, x_2);

  // Other names for the same wires on the sheet: x_t = x_2

  // Notes on the sheet:
  //   Sequencia: 110
  //   Sequencia correta: 1101
endmodule

module Q04 (
  input  x,
  output out_2
);

  wire clock_1_out, d_ff_1_q, d_ff_2_q, d_ff_3_q, d_ff_4_q, not_1_out, not_2_out, not_3_out;

  Clock clock_1 (.out(clock_1_out));
  D_Flip_Flop #(.Pre_Clr_Positions("LEGACY"), .enable("true"), .NewFFLayout("false")) d_ff_1 (
    .clk(clock_1_out), .D(x), .Q(d_ff_1_q), .en(not_3_out));  // open: Qn, preset, reset
  D_Flip_Flop #(.Pre_Clr_Positions("LEGACY"), .enable("true"), .NewFFLayout("false")) d_ff_2 (
    .clk(clock_1_out), .D(d_ff_1_q), .Q(d_ff_2_q), .en(not_3_out));  // open: Qn, preset, reset
  D_Flip_Flop #(.Pre_Clr_Positions("LEGACY"), .enable("true"), .NewFFLayout("false")) d_ff_3 (
    .clk(clock_1_out), .D(d_ff_2_q), .Q(d_ff_3_q), .en(not_3_out));  // open: Qn, preset, reset
  D_Flip_Flop #(.Pre_Clr_Positions("LEGACY"), .enable("true"), .NewFFLayout("false")) d_ff_4 (
    .clk(clock_1_out), .D(d_ff_3_q), .Q(d_ff_4_q), .en(not_3_out));  // open: Qn, preset, reset
  not not_1 (not_1_out, d_ff_3_q);
  not not_2 (not_2_out, d_ff_2_q);
  and and_1 (out_2, d_ff_4_q, not_1_out, not_2_out, d_ff_1_q);
  not not_3 (not_3_out, out_2);
endmodule

module Q05 (
  input  x,
  output saida
);

  wire and_1_out, and_2_out, and_4_out, and_5_out, and_6_out, clk, found, not_1_out, not_2_out, not_3_out,
       not_4_out, not_5_out, not_6_out, not_7_out, not_8_out, not_10_out, not_11_out, not_12_out, not_13_out,
       not_14_out, not_15_out, not_16_out, or_1_out, or_2_out, q0, q1, q2;

  Clock clock_1 (.out(clk));
  not not_1 (not_1_out, q2);
  not not_2 (not_2_out, q1);
  and and_1 (and_1_out, not_1_out, not_2_out, q0, not_3_out);
  not not_3 (not_3_out, x);
  not not_4 (not_4_out, q2);
  and and_2 (and_2_out, not_4_out, q1, not_5_out, not_6_out);
  not not_5 (not_5_out, q0);
  not not_6 (not_6_out, x);
  not not_7 (not_7_out, q1);
  not not_8 (not_8_out, q2);
  or or_1 (or_1_out, and_1_out, and_2_out);
  and and_3 (saida, q0, not_7_out, not_8_out, x);
  not not_9 (found, saida);
  D_Flip_Flop #(.Pre_Clr_Positions("LEGACY"), .enable("true"), .NewFFLayout("false")) d_ff_1 (
    .clk(clk), .D(or_1_out), .Q(q1), .en(found));  // open: Qn, preset, reset
  not not_10 (not_10_out, q2);
  and and_4 (and_4_out, not_10_out, q1, q0, x);
  not not_11 (not_11_out, q2);
  not not_12 (not_12_out, q1);
  not not_13 (not_13_out, x);
  not not_14 (not_14_out, q2);
  not not_15 (not_15_out, q1);
  not not_16 (not_16_out, q0);
  D_Flip_Flop #(.Pre_Clr_Positions("LEGACY"), .enable("true"), .NewFFLayout("false")) d_ff_2 (
    .clk(clk), .D(and_4_out), .Q(q2), .en(found));  // open: Qn, preset, reset
  and and_5 (and_5_out, not_11_out, not_12_out, q0, not_13_out);
  or or_2 (or_2_out, and_5_out, and_6_out);
  and and_6 (and_6_out, not_14_out, not_15_out, not_16_out, x);
  D_Flip_Flop #(.Pre_Clr_Positions("LEGACY"), .enable("true"), .NewFFLayout("false")) d_ff_3 (
    .clk(clk), .D(or_2_out), .Q(q0), .en(found));  // open: Qn, preset, reset

  // Notes on the sheet:
  //   Nao consegui fazer a sequencia ser detectada apenas 1 vez.
endmodule

module Q06 (
  input  x,
  output saida
);

  wire and_1_out, and_2_out, and_4_out, and_5_out, and_6_out, clk, not_1_out, not_2_out, not_3_out,
       not_4_out, not_5_out, not_6_out, not_7_out, not_8_out, not_9_out, not_10_out, not_11_out, not_12_out,
       not_13_out, not_14_out, not_15_out, or_1_out, or_2_out, q0, q1, q2;

  Clock clock_1 (.out(clk));
  not not_1 (not_1_out, q2);
  not not_2 (not_2_out, q1);
  and and_1 (and_1_out, not_1_out, not_2_out, q0, not_3_out);
  not not_3 (not_3_out, x);
  not not_4 (not_4_out, q2);
  and and_2 (and_2_out, not_4_out, q1, not_5_out, not_6_out);
  not not_5 (not_5_out, q0);
  not not_6 (not_6_out, x);
  not not_7 (not_7_out, q1);
  not not_8 (not_8_out, q2);
  or or_1 (or_1_out, and_1_out, and_2_out);
  and and_3 (saida, q0, not_7_out, not_8_out, x);
  D_Flip_Flop #(.Pre_Clr_Positions("LEGACY"), .enable("true"), .NewFFLayout("false")) d_ff_1 (
    .clk(clk), .D(or_1_out), .Q(q1));  // open: Qn, preset, en, reset
  not not_9 (not_9_out, q2);
  and and_4 (and_4_out, not_9_out, q1, q0, x);
  not not_10 (not_10_out, q2);
  not not_11 (not_11_out, q1);
  not not_12 (not_12_out, x);
  not not_13 (not_13_out, q2);
  not not_14 (not_14_out, q1);
  not not_15 (not_15_out, q0);
  D_Flip_Flop #(.Pre_Clr_Positions("LEGACY"), .enable("true"), .NewFFLayout("false")) d_ff_2 (
    .clk(clk), .D(and_4_out), .Q(q2));  // open: Qn, preset, en, reset
  and and_5 (and_5_out, not_10_out, not_11_out, q0, not_12_out);
  or or_2 (or_2_out, and_5_out, and_6_out);
  and and_6 (and_6_out, not_13_out, not_14_out, not_15_out, x);
  D_Flip_Flop #(.Pre_Clr_Positions("LEGACY"), .enable("true"), .NewFFLayout("false")) d_ff_3 (
    .clk(clk), .D(or_2_out), .Q(q0));  // open: Qn, preset, en, reset
endmodule

module Q07 (
  input  x,
  output out_2
);

  wire clock_1_out, d_ff_1_q, d_ff_2_q, d_ff_3_q, d_ff_4_q, not_1_out, not_2_out, not_3_out;

  Clock clock_1 (.out(clock_1_out));
  D_Flip_Flop #(.Pre_Clr_Positions("LEGACY"), .enable("true"), .NewFFLayout("false")) d_ff_1 (
    .clk(clock_1_out), .D(x), .Q(d_ff_1_q));  // open: Qn, preset, en, reset
  D_Flip_Flop #(.Pre_Clr_Positions("LEGACY"), .enable("true"), .NewFFLayout("false")) d_ff_2 (
    .clk(clock_1_out), .D(d_ff_1_q), .Q(d_ff_2_q));  // open: Qn, preset, en, reset
  D_Flip_Flop #(.Pre_Clr_Positions("LEGACY"), .enable("true"), .NewFFLayout("false")) d_ff_3 (
    .clk(clock_1_out), .D(d_ff_2_q), .Q(d_ff_3_q));  // open: Qn, preset, en, reset
  D_Flip_Flop #(.Pre_Clr_Positions("LEGACY"), .enable("true"), .NewFFLayout("false")) d_ff_4 (
    .clk(clock_1_out), .D(d_ff_3_q), .Q(d_ff_4_q));  // open: Qn, preset, en, reset
  not not_1 (not_1_out, d_ff_4_q);
  not not_2 (not_2_out, d_ff_3_q);
  not not_3 (not_3_out, d_ff_2_q);
  and and_1 (out_2, not_1_out, not_2_out, not_3_out);
endmodule

module Q08 (
  input  x,
  output Saida
);

  wire a, and_1_out, and_2_out, b, c, clock_1_out, not_1_out, not_2_out, not_3_out;

  Clock clock_1 (.out(clock_1_out));
  D_Flip_Flop #(.Pre_Clr_Positions("LEGACY"), .enable("true"), .NewFFLayout("false")) d_ff_1 (
    .clk(clock_1_out), .D(x), .Q(c));  // open: Qn, preset, en, reset
  D_Flip_Flop #(.Pre_Clr_Positions("LEGACY"), .enable("true"), .NewFFLayout("false")) d_ff_2 (
    .clk(clock_1_out), .D(c), .Q(b));  // open: Qn, preset, en, reset
  not not_1 (not_1_out, a);
  and and_1 (and_1_out, not_1_out, b, not_2_out);
  not not_2 (not_2_out, c);
  not not_3 (not_3_out, b);
  and and_2 (and_2_out, a, not_3_out, c);
  D_Flip_Flop #(.Pre_Clr_Positions("LEGACY"), .enable("true"), .NewFFLayout("false")) d_ff_3 (
    .clk(clock_1_out), .D(b), .Q(a));  // open: Qn, preset, en, reset
  or or_1 (Saida, and_1_out, and_2_out);
endmodule
