// Logisim project Guia_17.circ as structural Verilog: 3 circuits, main circuit 1701
module _1701 (
  input  a,
  input  b,
  output t_1,
  output t_1_2
);

  wire clock_1_out, clock_2_out;

  Clock clock_1 (.out(clock_1_out));
  D_Flip_Flop #(.Pre_Clr_Positions("LEGACY"), .NewFFLayout("false")) d_ff_1 (
    .clk(clock_1_out), .D(a), .Q(t_1));  // open: Qn, preset, reset
  Clock clock_2 (.out(clock_2_out));
  D_Flip_Flop #(.Pre_Clr_Positions("LEGACY"), .NewFFLayout("false")) d_ff_2 (
    .clk(clock_2_out), .D(b), .Q(t_1_2));  // open: Qn, preset, reset
endmodule

module _1704 (
  input  clr,
  output out_2,
  output out_3,
  output out_4,
  output out_5,
  output out_6
);

  wire clock_1_out, t_ff_1_q, t_ff_2_q, t_ff_3_q, t_ff_4_q, t_ff_5_q;

  Clock clock_1 (.out(clock_1_out));
  not not_1 (out_2, t_ff_5_q);
  T_Flip_Flop #(.Pre_Clr_Positions("LEGACY"), .NewFFLayout("false")) t_ff_1 (
    .clk(clock_1_out), .T(1'b1), .Q(t_ff_1_q), .preset(clr));  // open: Qn, reset
  not not_2 (out_6, t_ff_1_q);
  not not_3 (out_3, t_ff_4_q);
  not not_4 (out_5, t_ff_2_q);
  not not_5 (out_4, t_ff_3_q);
  T_Flip_Flop #(.Pre_Clr_Positions("LEGACY"), .NewFFLayout("false")) t_ff_2 (
    .clk(t_ff_1_q), .T(1'b1), .Q(t_ff_2_q), .preset(clr));  // open: Qn, reset
  T_Flip_Flop #(.Pre_Clr_Positions("LEGACY"), .NewFFLayout("false")) t_ff_3 (
    .clk(t_ff_2_q), .T(1'b1), .Q(t_ff_3_q), .preset(clr));  // open: Qn, reset
  T_Flip_Flop #(.Pre_Clr_Positions("LEGACY"), .NewFFLayout("false")) t_ff_4 (
    .clk(t_ff_3_q), .T(1'b1), .Q(t_ff_4_q), .preset(clr));  // open: Qn, reset
  T_Flip_Flop #(.Pre_Clr_Positions("LEGACY"), .NewFFLayout("false")) t_ff_5 (
    .clk(t_ff_4_q), .T(1'b1), .Q(t_ff_5_q), .preset(clr));  // open: Qn, reset
endmodule

module _1705 (
  input  clr,
  output out_2,
  output out_3,
  output out_4,
  output out_5,
  output out_6
);

  wire clock_1_out, t_ff_1_qn, t_ff_2_qn, t_ff_3_qn, t_ff_4_qn;

  Clock clock_1 (.out(clock_1_out));
  T_Flip_Flop #(.Pre_Clr_Positions("LEGACY"), .NewFFLayout("false")) t_ff_1 (
    .clk(clock_1_out), .T(1'b1), .Q(out_6), .Qn(t_ff_1_qn), .reset(clr));  // open: preset
  T_Flip_Flop #(.Pre_Clr_Positions("LEGACY"), .NewFFLayout("false")) t_ff_2 (
    .clk(t_ff_1_qn), .T(1'b1), .Q(out_5), .Qn(t_ff_2_qn), .reset(clr));  // open: preset
  T_Flip_Flop #(.Pre_Clr_Positions("LEGACY"), .NewFFLayout("false")) t_ff_3 (
    .clk(t_ff_2_qn), .T(1'b1), .Q(out_4), .Qn(t_ff_3_qn), .reset(clr));  // open: preset
  T_Flip_Flop #(.Pre_Clr_Positions("LEGACY"), .NewFFLayout("false")) t_ff_4 (
    .clk(t_ff_3_qn), .T(1'b1), .Q(out_3), .Qn(t_ff_4_qn), .reset(clr));  // open: preset
  T_Flip_Flop #(.Pre_Clr_Positions("LEGACY"), .NewFFLayout("false")) t_ff_5 (
    .clk(t_ff_4_qn), .T(1'b1), .Q(out_2), .reset(clr));  // open: Qn, preset
endmodule
